// Logisim project Screen.circ as structural Verilog: 1 circuit, main circuit main
module main (
  input  Refresh,
  input  Reset,
  input  [15:0] Data,
  input  [3:0] Address,
  input  Write,
  output [15:0] out_6,
  output [15:0] out_7,
  output [15:0] out_8,
  output [15:0] out_9,
  output [15:0] out_10,
  output [15:0] out_11,
  output [15:0] out_12,
  output [15:0] out_13,
  output [15:0] out_14,
  output [15:0] out_15,
  output [15:0] out_16,
  output [15:0] out_17,
  output [15:0] out_18,
  output [15:0] out_19,
  output [15:0] out_20,
  output [15:0] out_21
);

  wire demultiplexer_1_out0, demultiplexer_1_out1, demultiplexer_1_out2, demultiplexer_1_out3,
       demultiplexer_1_out4, demultiplexer_1_out5, demultiplexer_1_out6, demultiplexer_1_out7,
       demultiplexer_1_out8, demultiplexer_1_out9, demultiplexer_1_out10, demultiplexer_1_out11,
       demultiplexer_1_out12, demultiplexer_1_out13, demultiplexer_1_out14, demultiplexer_1_out15;
  wire [15:0] register_1_q, register_3_q, register_6_q, register_8_q, register_10_q, register_11_q,
       register_14_q, register_15_q, register_17_q, register_20_q, register_22_q, register_23_q,
       register_26_q, register_27_q, register_29_q, register_31_q;

  Demultiplexer #(.select(4), .enable("false")) demultiplexer_1 (
    .out0(demultiplexer_1_out0), .out1(demultiplexer_1_out1), .out2(demultiplexer_1_out2),
    .out3(demultiplexer_1_out3), .out4(demultiplexer_1_out4), .out5(demultiplexer_1_out5),
    .out6(demultiplexer_1_out6), .out7(demultiplexer_1_out7), .out8(demultiplexer_1_out8),
    .out9(demultiplexer_1_out9), .out10(demultiplexer_1_out10), .out11(demultiplexer_1_out11),
    .out12(demultiplexer_1_out12), .out13(demultiplexer_1_out13), .out14(demultiplexer_1_out14),
    .out15(demultiplexer_1_out15), .in(Write), .sel(Address));
  Register #(.width(16)) register_1 (.D(Data), .Q(register_1_q), .clk(demultiplexer_1_out0), .clr(Reset));  // open: en
  Register #(.width(16)) register_2 (.D(register_1_q), .Q(out_6), .clk(Refresh), .clr(Reset));  // open: en
  Register #(.width(16)) register_3 (.D(Data), .Q(register_3_q), .clk(demultiplexer_1_out1), .clr(Reset));  // open: en
  Register #(.width(16)) register_4 (.D(register_3_q), .Q(out_7), .clk(Refresh), .clr(Reset));  // open: en
  Register #(.width(16)) register_5 (.D(register_6_q), .Q(out_8), .clk(Refresh), .clr(Reset));  // open: en
  Register #(.width(16)) register_6 (.D(Data), .Q(register_6_q), .clk(demultiplexer_1_out2), .clr(Reset));  // open: en
  Register #(.width(16)) register_7 (.D(register_8_q), .Q(out_9), .clk(Refresh), .clr(Reset));  // open: en
  Register #(.width(16)) register_8 (.D(Data), .Q(register_8_q), .clk(demultiplexer_1_out3), .clr(Reset));  // open: en
  Register #(.width(16)) register_9 (.D(register_10_q), .Q(out_10), .clk(Refresh), .clr(Reset));  // open: en
  Register #(.width(16)) register_10 (
    .D(Data), .Q(register_10_q), .clk(demultiplexer_1_out4), .clr(Reset));  // open: en
  Register #(.width(16)) register_11 (
    .D(Data), .Q(register_11_q), .clk(demultiplexer_1_out5), .clr(Reset));  // open: en
  Register #(.width(16)) register_12 (.D(register_11_q), .Q(out_11), .clk(Refresh), .clr(Reset));  // open: en
  Register #(.width(16)) register_13 (.D(register_14_q), .Q(out_12), .clk(Refresh), .clr(Reset));  // open: en
  Register #(.width(16)) register_14 (
    .D(Data), .Q(register_14_q), .clk(demultiplexer_1_out6), .clr(Reset));  // open: en
  Register #(.width(16)) register_15 (
    .D(Data), .Q(register_15_q), .clk(demultiplexer_1_out7), .clr(Reset));  // open: en
  Register #(.width(16)) register_16 (.D(register_15_q), .Q(out_13), .clk(Refresh), .clr(Reset));  // open: en
  Register #(.width(16)) register_17 (
    .D(Data), .Q(register_17_q), .clk(demultiplexer_1_out8), .clr(Reset));  // open: en
  Register #(.width(16)) register_18 (.D(register_17_q), .Q(out_14), .clk(Refresh), .clr(Reset));  // open: en
  Register #(.width(16)) register_19 (.D(register_20_q), .Q(out_15), .clk(Refresh), .clr(Reset));  // open: en
  Register #(.width(16)) register_20 (
    .D(Data), .Q(register_20_q), .clk(demultiplexer_1_out9), .clr(Reset));  // open: en
  Register #(.width(16)) register_21 (.D(register_22_q), .Q(out_16), .clk(Refresh), .clr(Reset));  // open: en
  Register #(.width(16)) register_22 (
    .D(Data), .Q(register_22_q), .clk(demultiplexer_1_out10), .clr(Reset));  // open: en
  Register #(.width(16)) register_23 (
    .D(Data), .Q(register_23_q), .clk(demultiplexer_1_out11), .clr(Reset));  // open: en
  Register #(.width(16)) register_24 (.D(register_23_q), .Q(out_17), .clk(Refresh), .clr(Reset));  // open: en
  Register #(.width(16)) register_25 (.D(register_26_q), .Q(out_18), .clk(Refresh), .clr(Reset));  // open: en
  Register #(.width(16)) register_26 (
    .D(Data), .Q(register_26_q), .clk(demultiplexer_1_out12), .clr(Reset));  // open: en
  Register #(.width(16)) register_27 (
    .D(Data), .Q(register_27_q), .clk(demultiplexer_1_out13), .clr(Reset));  // open: en
  Register #(.width(16)) register_28 (.D(register_27_q), .Q(out_19), .clk(Refresh), .clr(Reset));  // open: en
  Register #(.width(16)) register_29 (
    .D(Data), .Q(register_29_q), .clk(demultiplexer_1_out14), .clr(Reset));  // open: en
  Register #(.width(16)) register_30 (.D(register_29_q), .Q(out_20), .clk(Refresh), .clr(Reset));  // open: en
  Register #(.width(16)) register_31 (
    .D(Data), .Q(register_31_q), .clk(demultiplexer_1_out15), .clr(Reset));  // open: en
  Register #(.width(16)) register_32 (.D(register_31_q), .Q(out_21), .clk(Refresh), .clr(Reset));  // open: en
endmodule
